# Fritzing sketch senseo-api-board-example (saved by Fritzing 0.9.3b)
breadboards: 1

parts:
  Raspberry_Pi_1 = Raspberry Pi 3 [part_number=RPI-3-V1.2]
  S3 = Pushbutton [package="[THT]"]
  LED1 = LED - 5mm [color="Red (633nm)" package="5 mm [THT]"]
  S2 = Pushbutton [package="[THT]"]
  S1 = Pushbutton [part_number="Power ON" package="[THT]"]
  Composant1 = I2C level shifter bidirectional
  R1 = Resistor [tolerance=±5% resistance=220 package=THT]

nets:
  N1: Raspberry_Pi_1.3v3, Composant1.LV
  N2: Raspberry_Pi_1.GPIO4, Composant1.LV1
  GND: Raspberry_Pi_1.GND, S3.Pin_3, S3.Pin_4, LED1.cathode, S2.Pin_3, S2.Pin_4, S1.Pin_3, S1.Pin_4, Composant1.GND
  N3: Raspberry_Pi_1.GPIO17, Composant1.LV2
  N4: Raspberry_Pi_1.GPIO27, Composant1.LV3
  N5: Raspberry_Pi_1.GPIO22, Composant1.LV4
  N6: Raspberry_Pi_1.5V, Composant1.HV
  N7: S3.Pin_1, S3.Pin_2, Composant1.HV4
  N8: LED1.anode, R1.Pin_1
  N9: S2.Pin_1, S2.Pin_2, Composant1.HV2
  N10: S1.Pin_1, S1.Pin_2, Composant1.HV1
  N11: Composant1.HV3, R1.Pin_0

notes:
  Power ON
  1 mug
  2 mugs
